# Fritzing sketch 8266-st7789-mqtt (saved by Fritzing 0.9.3b)
breadboards: 1

parts:
  Part1 = Adafruit 2.0 inch 240x320 IPS TFT [part_number="Adafruit #4311"]
  U1 = NodeMCU V3.0

nets:
  N1: Part1.DC_5V, U1.D1
  N2: Part1.RESET_5V, U1.D0
  N3: Part1.LCDCS_5V, U1.D2
  N4: Part1.MOSI_5V, U1.D7
  N5: Part1.SCLK_5V, U1.D5
  N6: Part1.GND, U1.GND#6, U1.GND#13, U1.GND#16, U1.GND#33
  VIN: Part1.VIN, U1.3V3

notes:
  8266 NodeMcu - ST7789 2.0" ISP TFT Display
  Using MQTT, WiFi
  NodeMCU design by:
  roman-minyaylov
  /
  fritzing-parts (on GitHub)

custom parts:
  Adafruit 2.0 inch 240x320 IPS TFT: This gorgeous IPS display breakout is the best way to add a small, colorful and bright display to any project, with excellent visibility from any angle. Since the display uses 4-wire SPI to communicate and has its own pixel-addressable frame buffer, it can be used with every kind of microcontroller. Even a very small one with low memory and few pins available! The 2.0" display has 320x240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
  NodeMCU V3.0: ESP8266 based NodeMCU
